# Fritzing sketch OpticFC_noGyroAccel (saved by Fritzing 0.9.3b)
breadboards: 1

parts:
  Main_Arduino_UNO = Arduino Uno (Rev3)
  IC1 = IC, DIP package, 10 pins [chip_label=FS-iA6B]
  LED1 = smd LED [color="Red (635nm)" package="0603 [SMD]"]
  Lipo = LIPO-2000mAh [part_number=LIPO package=lipo-2000]
  U4 = mystery part, 4 pins [chip_label=ESC]
  U5 = mystery part, 4 pins [chip_label=ESC]
  U6 = mystery part, 4 pins [chip_label=ESC]
  U7 = mystery part, 4 pins [chip_label=ESC]

nets:
  N1: Main_Arduino_UNO.D8, IC1.pin2
  N2: Main_Arduino_UNO.D9_PWM, U6.pin2
  N3: Main_Arduino_UNO.D10_PWM/SS, U5.pin2
  N4: Main_Arduino_UNO.D11_PWM/MOSI, U4.pin2
  N5: Main_Arduino_UNO.D12/MISO, IC1.pin1
  N6: Main_Arduino_UNO.D13/SCK, IC1.pin10
  N7: Main_Arduino_UNO.GND, IC1.pin6, IC1.pin7, LED1.cathode, U4.pin3, U5.pin3, U6.pin3, U7.pin3
  N8: Main_Arduino_UNO.D2, IC1.pin5
  N9: Main_Arduino_UNO.D4, IC1.pin4
  N10: Main_Arduino_UNO.D5_PWM, LED1.anode
  N11: Main_Arduino_UNO.D6_PWM, U7.pin2
  N12: Main_Arduino_UNO.D7, IC1.pin3
  N13: Main_Arduino_UNO.5V, IC1.pin8
  N14: Lipo.+, U4.pin1, U5.pin1, U6.pin1, U7.pin1
  N15: Lipo.-, U4.pin4, U5.pin4, U6.pin4, U7.pin4
